// Logisim project 3.circ as structural Verilog: 1 circuit, main circuit main
module main (
  input  in_1,
  input  in_2,
  input  in_3,
  output out_4,
  output out_5,
  output out_6,
  output out_7,
  output out_8
);

  wire and_1_out, and_2_out, clock_1_out;

  Clock clock_1 (.out(clock_1_out));
  J_K_Flip_Flop j_k_ff_1 (.J(in_1), .clk(clock_1_out), .K(out_8), .Q(out_8), .en(in_3));  // open: Qn, preset, reset
  J_K_Flip_Flop j_k_ff_2 (.J(in_2), .clk(clock_1_out), .K(in_2), .Q(out_7), .en(in_3));  // open: Qn, preset, reset
  J_K_Flip_Flop j_k_ff_3 (.J(out_7), .clk(clock_1_out), .K(out_7), .Q(out_6), .en(in_3));  // open: Qn, preset, reset
  and and_1 (and_1_out, out_6, out_7);
  J_K_Flip_Flop j_k_ff_4 (
    .J(and_1_out), .clk(clock_1_out), .K(and_1_out), .Q(out_5), .en(in_3));  // open: Qn, preset, reset
  and and_2 (and_2_out, out_5, and_1_out);
  J_K_Flip_Flop j_k_ff_5 (
    .J(and_2_out), .clk(clock_1_out), .K(and_2_out), .Q(out_4), .en(in_3));  // open: Qn, preset, reset

  // Notes on the sheet:
  //   A
  //   B
  //   C
  //   D
  //   E
endmodule
